// Logisim project alu.circ as structural Verilog: 14 circuits, main circuit main
module main (
  input  [2:0] s,
  input  [7:0] a,
  input  [7:0] b,
  output [7:0] r,
  output overflow
);

  // Probe on a
  // Probe on b
  ALU alu_1 (
    .a7(a[7]), .a6(a[6]), .a5(a[5]), .a4(a[4]), .a3(a[3]), .a2(a[2]), .a1(a[1]), .a0(a[0]), .b7(b[7]),
    .b6(b[6]), .b5(b[5]), .b4(b[4]), .b3(b[3]), .b2(b[2]), .b1(b[1]), .b0(b[0]), .r7(r[7]), .r6(r[6]),
    .r5(r[5]), .r4(r[4]), .r3(r[3]), .r2(r[2]), .r1(r[1]), .r0(r[0]), .overflow(overflow), .s2(s[2]),
    .s1(s[1]), .s0(s[0]));
  // Probe on r
endmodule

module ALU (
  input  a7,
  input  a6,
  input  a5,
  input  a4,
  input  a3,
  input  a2,
  input  a1,
  input  a0,
  input  b7,
  input  b6,
  input  b5,
  input  b4,
  input  b3,
  input  b2,
  input  b1,
  input  b0,
  input  s2,
  input  s1,
  input  s0,
  output r7,
  output r6,
  output r5,
  output r4,
  output r3,
  output r2,
  output r1,
  output r0,
  output overflow
);

  wire n8_bit_adder_1_overflow, n8_bit_divider_1_overflow, n8_bit_multiplicator_1_overflow,
       n8_bit_subtractor_1_overflow;
  wire [7:0] n8_bit_adder_1_a_b, n8_bit_divider_1_quotient_of_a_b, n8_bit_divider_1_remainder_of_a_b,
       n8_bit_multiplicator_1_a_x_b, n8_bit_subtractor_1_a_b;

  Multiplexer #(.select(3)) multiplexer_1 (
    .in0(n8_bit_adder_1_overflow), .in1(n8_bit_subtractor_1_overflow), .in2(n8_bit_multiplicator_1_overflow),
    .in3(n8_bit_divider_1_overflow), .in4(n8_bit_divider_1_overflow), .out(overflow), .sel({s2, s1, s0}));  // open: in5, in6, in7, en
  _8_bit_adder u_8_bit_adder_1 (
    .a({a7, a6, a5, a4, a3, a2, a1, a0}), .b({b7, b6, b5, b4, b3, b2, b1, b0}),
    .overflow(n8_bit_adder_1_overflow), .a_b(n8_bit_adder_1_a_b));
  _8_bit_subtractor u_8_bit_subtractor_1 (
    .a({a7, a6, a5, a4, a3, a2, a1, a0}), .b({b7, b6, b5, b4, b3, b2, b1, b0}),
    .overflow(n8_bit_subtractor_1_overflow), .a_b(n8_bit_subtractor_1_a_b));
  _8_bit_multiplicator u_8_bit_multiplicator_1 (
    .a({a7, a6, a5, a4, a3, a2, a1, a0}), .b({b7, b6, b5, b4, b3, b2, b1, b0}),
    .overflow(n8_bit_multiplicator_1_overflow), .a_x_b(n8_bit_multiplicator_1_a_x_b));
  _8_bit_divider u_8_bit_divider_1 (
    .a({a7, a6, a5, a4, a3, a2, a1, a0}), .b({b7, b6, b5, b4, b3, b2, b1, b0}),
    .overflow(n8_bit_divider_1_overflow), .quotient_of_a_b(n8_bit_divider_1_quotient_of_a_b),
    .remainder_of_a_b(n8_bit_divider_1_remainder_of_a_b));
  Multiplexer #(.select(3), .width(8)) multiplexer_2 (
    .in0(n8_bit_adder_1_a_b), .in1(n8_bit_subtractor_1_a_b), .in2(n8_bit_multiplicator_1_a_x_b),
    .in3(n8_bit_divider_1_quotient_of_a_b), .in4(n8_bit_divider_1_remainder_of_a_b),
    .out({r7, r6, r5, r4, r3, r2, r1, r0}), .sel({s2, s1, s0}));  // open: in5, in6, in7, en
endmodule

// HA
module Half_adder (
  input  a,
  input  b,
  output cout,
  output sum
);

  and and_1 (cout, a, b);
  xor xor_1 (sum, a, b);
endmodule

// FA
module Full_adder (
  input  a,
  input  b,
  input  cin,
  output cout,
  output sum
);

  wire and_1_out, and_2_out, xor_1_out;

  xor xor_1 (xor_1_out, b, cin);
  xor xor_2 (sum, a, xor_1_out);
  and and_1 (and_1_out, a, xor_1_out);
  and and_2 (and_2_out, b, cin);
  or or_1 (cout, and_1_out, and_2_out);
endmodule

// ADD
module _8_bit_adder (
  input  [7:0] a,
  input  [7:0] b,
  output overflow,
  output [7:0] a_b
);

  wire full_adder_1_cout, full_adder_2_cout, full_adder_3_cout, full_adder_4_cout, full_adder_5_cout,
       full_adder_6_cout, full_adder_7_cout, half_adder_1_cout;

  // Probe on b
  // Probe on a
  xor xor_1 (overflow, full_adder_1_cout, full_adder_2_cout);
  Full_adder full_adder_1 (.a(a[7]), .b(b[7]), .cout(full_adder_1_cout), .cin(full_adder_2_cout), .sum(a_b[7]));
  Full_adder full_adder_2 (.a(a[6]), .b(b[6]), .cout(full_adder_2_cout), .cin(full_adder_3_cout), .sum(a_b[6]));
  Full_adder full_adder_3 (.a(a[5]), .b(b[5]), .cout(full_adder_3_cout), .cin(full_adder_4_cout), .sum(a_b[5]));
  Full_adder full_adder_4 (.a(a[4]), .b(b[4]), .cout(full_adder_4_cout), .cin(full_adder_5_cout), .sum(a_b[4]));
  Full_adder full_adder_5 (.a(a[3]), .b(b[3]), .cout(full_adder_5_cout), .cin(full_adder_6_cout), .sum(a_b[3]));
  Full_adder full_adder_6 (.a(a[2]), .b(b[2]), .cout(full_adder_6_cout), .cin(full_adder_7_cout), .sum(a_b[2]));
  Full_adder full_adder_7 (.a(a[1]), .b(b[1]), .cout(full_adder_7_cout), .cin(half_adder_1_cout), .sum(a_b[1]));
  Half_adder half_adder_1 (.a(a[0]), .b(b[0]), .cout(half_adder_1_cout), .sum(a_b[0]));
  // Probe on a_b
endmodule

// 2C
module _2_s_complement (
  input  [7:0] a,
  output [7:0] minus_a
);

  wire half_adder_2_cout, half_adder_3_cout, half_adder_4_cout, half_adder_5_cout, half_adder_6_cout,
       half_adder_7_cout, half_adder_8_cout, not_1_out, not_2_out, not_3_out, not_4_out, not_5_out,
       not_6_out, not_7_out, not_8_out;

  // Probe on a
  not not_1 (not_1_out, a[7]);
  not not_2 (not_2_out, a[6]);
  not not_3 (not_3_out, a[5]);
  not not_4 (not_4_out, a[4]);
  not not_5 (not_5_out, a[3]);
  not not_6 (not_6_out, a[2]);
  not not_7 (not_7_out, a[1]);
  not not_8 (not_8_out, a[0]);
  Half_adder half_adder_1 (.a(not_1_out), .b(half_adder_2_cout), .sum(minus_a[7]));  // open: cout
  Half_adder half_adder_2 (.a(not_2_out), .b(half_adder_3_cout), .cout(half_adder_2_cout), .sum(minus_a[6]));
  Half_adder half_adder_3 (.a(not_3_out), .b(half_adder_4_cout), .cout(half_adder_3_cout), .sum(minus_a[5]));
  Half_adder half_adder_4 (.a(not_4_out), .b(half_adder_5_cout), .cout(half_adder_4_cout), .sum(minus_a[4]));
  Half_adder half_adder_5 (.a(not_5_out), .b(half_adder_6_cout), .cout(half_adder_5_cout), .sum(minus_a[3]));
  Half_adder half_adder_6 (.a(not_6_out), .b(half_adder_7_cout), .cout(half_adder_6_cout), .sum(minus_a[2]));
  Half_adder half_adder_7 (.a(not_7_out), .b(half_adder_8_cout), .cout(half_adder_7_cout), .sum(minus_a[1]));
  Half_adder half_adder_8 (.a(not_8_out), .b(1'b1), .cout(half_adder_8_cout), .sum(minus_a[0]));
  // Probe on minus_a
endmodule

// SUB
module _8_bit_subtractor (
  input  [7:0] a,
  input  [7:0] b,
  output overflow,
  output [7:0] a_b
);

  wire [7:0] n2_s_complement_1_minus_a;

  // Probe on a
  // Probe on b
  _2_s_complement u_2_s_complement_1 (.a(b), .minus_a(n2_s_complement_1_minus_a));
  _8_bit_adder u_8_bit_adder_1 (.a(a), .b(n2_s_complement_1_minus_a), .overflow(overflow), .a_b(a_b));
  // Probe on a_b
endmodule

// MUL
module _8_bit_multiplicator (
  input  [7:0] a,
  input  [7:0] b,
  output overflow,
  output [7:0] a_x_b
);

  wire n8_bit_adder_1_overflow, n8_bit_adder_2_overflow, n8_bit_adder_3_overflow, n8_bit_adder_4_overflow,
       n8_bit_adder_5_overflow, n8_bit_adder_6_overflow, n8_bit_adder_7_overflow,
       n8_bit_left_shift_3_overflow, n8_bit_left_shift_5_overflow, n8_bit_left_shift_6_overflow,
       n8_bit_left_shift_7_overflow, n8_bit_left_shift_8_overflow, n8_bit_left_shift_9_overflow,
       n8_bit_left_shift_10_overflow, n8_bit_left_shift_11_overflow, n8_bit_left_shift_12_overflow,
       n8_bit_left_shift_13_overflow, n8_bit_left_shift_14_overflow, n8_bit_left_shift_15_overflow,
       n8_bit_left_shift_16_overflow, n8_bit_left_shift_17_overflow, n8_bit_left_shift_18_overflow,
       n8_bit_left_shift_21_overflow, n8_bit_left_shift_23_overflow, n8_bit_left_shift_24_overflow,
       n8_bit_left_shift_25_overflow, n8_bit_left_shift_26_overflow, n8_bit_left_shift_27_overflow, or_1_out,
       or_2_out, OV_1, OV_2, OV_3, OV_4, OV_5, OV_6, OV_7, xor_1_out;
  wire [7:0] and_8_1_1_a_and_bbbbbbbb, and_8_1_2_a_and_bbbbbbbb, and_8_1_3_a_and_bbbbbbbb,
       and_8_1_4_a_and_bbbbbbbb, and_8_1_5_a_and_bbbbbbbb, and_8_1_6_a_and_bbbbbbbb,
       and_8_1_7_a_and_bbbbbbbb, and_8_1_8_a_and_bbbbbbbb, n2_s_complement_1_minus_a, n8_bit_absolute_1_a_2,
       n8_bit_absolute_2_a_2, n8_bit_adder_1_a_b, n8_bit_adder_2_a_b, n8_bit_adder_3_a_b, n8_bit_adder_4_a_b,
       n8_bit_adder_5_a_b, n8_bit_adder_6_a_b, n8_bit_adder_7_a_b, n8_bit_left_shift_1_a_left_shifted,
       n8_bit_left_shift_2_a_left_shifted, n8_bit_left_shift_3_a_left_shifted,
       n8_bit_left_shift_4_a_left_shifted, n8_bit_left_shift_5_a_left_shifted,
       n8_bit_left_shift_6_a_left_shifted, n8_bit_left_shift_7_a_left_shifted,
       n8_bit_left_shift_8_a_left_shifted, n8_bit_left_shift_9_a_left_shifted,
       n8_bit_left_shift_10_a_left_shifted, n8_bit_left_shift_11_a_left_shifted,
       n8_bit_left_shift_12_a_left_shifted, n8_bit_left_shift_13_a_left_shifted,
       n8_bit_left_shift_14_a_left_shifted, n8_bit_left_shift_15_a_left_shifted,
       n8_bit_left_shift_16_a_left_shifted, n8_bit_left_shift_17_a_left_shifted,
       n8_bit_left_shift_18_a_left_shifted, n8_bit_left_shift_19_a_left_shifted,
       n8_bit_left_shift_20_a_left_shifted, n8_bit_left_shift_21_a_left_shifted,
       n8_bit_left_shift_22_a_left_shifted, n8_bit_left_shift_23_a_left_shifted,
       n8_bit_left_shift_24_a_left_shifted, n8_bit_left_shift_25_a_left_shifted,
       n8_bit_left_shift_26_a_left_shifted, n8_bit_left_shift_27_a_left_shifted,
       n8_bit_left_shift_28_a_left_shifted;

  // Probe on a
  // Probe on b
  _8_bit_absolute u_8_bit_absolute_1 (.a(a), .a_2(n8_bit_absolute_1_a_2));
  _8_bit_absolute u_8_bit_absolute_2 (.a(b), .a_2(n8_bit_absolute_2_a_2));
  AND_8_1 and_8_1_1 (
    .a(n8_bit_absolute_1_a_2), .b(n8_bit_absolute_2_a_2[0]), .a_AND_bbbbbbbb(and_8_1_1_a_and_bbbbbbbb));
  AND_8_1 and_8_1_2 (
    .a(n8_bit_absolute_1_a_2), .b(n8_bit_absolute_2_a_2[1]), .a_AND_bbbbbbbb(and_8_1_2_a_and_bbbbbbbb));
  AND_8_1 and_8_1_3 (
    .a(n8_bit_absolute_1_a_2), .b(n8_bit_absolute_2_a_2[2]), .a_AND_bbbbbbbb(and_8_1_3_a_and_bbbbbbbb));
  AND_8_1 and_8_1_4 (
    .a(n8_bit_absolute_1_a_2), .b(n8_bit_absolute_2_a_2[3]), .a_AND_bbbbbbbb(and_8_1_4_a_and_bbbbbbbb));
  AND_8_1 and_8_1_5 (
    .a(n8_bit_absolute_1_a_2), .b(n8_bit_absolute_2_a_2[4]), .a_AND_bbbbbbbb(and_8_1_5_a_and_bbbbbbbb));
  AND_8_1 and_8_1_6 (
    .a(n8_bit_absolute_1_a_2), .b(n8_bit_absolute_2_a_2[5]), .a_AND_bbbbbbbb(and_8_1_6_a_and_bbbbbbbb));
  AND_8_1 and_8_1_7 (
    .a(n8_bit_absolute_1_a_2), .b(n8_bit_absolute_2_a_2[6]), .a_AND_bbbbbbbb(and_8_1_7_a_and_bbbbbbbb));
  AND_8_1 and_8_1_8 (
    .a(n8_bit_absolute_1_a_2), .b(n8_bit_absolute_2_a_2[7]), .a_AND_bbbbbbbb(and_8_1_8_a_and_bbbbbbbb));
  _8_bit_left_shift u_8_bit_left_shift_1 (
    .a(and_8_1_2_a_and_bbbbbbbb), .over_in(1'b0), .a_left_shifted(n8_bit_left_shift_1_a_left_shifted),
    .overflow(OV_1));
  _8_bit_left_shift u_8_bit_left_shift_2 (
    .a(n8_bit_left_shift_3_a_left_shifted), .over_in(n8_bit_left_shift_3_overflow),
    .a_left_shifted(n8_bit_left_shift_2_a_left_shifted), .overflow(OV_2));
  _8_bit_left_shift u_8_bit_left_shift_3 (
    .a(and_8_1_3_a_and_bbbbbbbb), .over_in(1'b0), .a_left_shifted(n8_bit_left_shift_3_a_left_shifted),
    .overflow(n8_bit_left_shift_3_overflow));
  _8_bit_left_shift u_8_bit_left_shift_4 (
    .a(n8_bit_left_shift_5_a_left_shifted), .over_in(n8_bit_left_shift_5_overflow),
    .a_left_shifted(n8_bit_left_shift_4_a_left_shifted), .overflow(OV_3));
  _8_bit_left_shift u_8_bit_left_shift_5 (
    .a(n8_bit_left_shift_6_a_left_shifted), .over_in(n8_bit_left_shift_6_overflow),
    .a_left_shifted(n8_bit_left_shift_5_a_left_shifted), .overflow(n8_bit_left_shift_5_overflow));
  _8_bit_left_shift u_8_bit_left_shift_6 (
    .a(and_8_1_4_a_and_bbbbbbbb), .over_in(1'b0), .a_left_shifted(n8_bit_left_shift_6_a_left_shifted),
    .overflow(n8_bit_left_shift_6_overflow));
  _8_bit_left_shift u_8_bit_left_shift_7 (
    .a(and_8_1_5_a_and_bbbbbbbb), .over_in(1'b0), .a_left_shifted(n8_bit_left_shift_7_a_left_shifted),
    .overflow(n8_bit_left_shift_7_overflow));
  _8_bit_left_shift u_8_bit_left_shift_8 (
    .a(n8_bit_left_shift_7_a_left_shifted), .over_in(n8_bit_left_shift_7_overflow),
    .a_left_shifted(n8_bit_left_shift_8_a_left_shifted), .overflow(n8_bit_left_shift_8_overflow));
  _8_bit_left_shift u_8_bit_left_shift_9 (
    .a(n8_bit_left_shift_8_a_left_shifted), .over_in(n8_bit_left_shift_8_overflow),
    .a_left_shifted(n8_bit_left_shift_9_a_left_shifted), .overflow(n8_bit_left_shift_9_overflow));
  _8_bit_left_shift u_8_bit_left_shift_10 (
    .a(n8_bit_left_shift_12_a_left_shifted), .over_in(n8_bit_left_shift_12_overflow),
    .a_left_shifted(n8_bit_left_shift_10_a_left_shifted), .overflow(n8_bit_left_shift_10_overflow));
  _8_bit_left_shift u_8_bit_left_shift_11 (
    .a(and_8_1_6_a_and_bbbbbbbb), .over_in(1'b0), .a_left_shifted(n8_bit_left_shift_11_a_left_shifted),
    .overflow(n8_bit_left_shift_11_overflow));
  _8_bit_left_shift u_8_bit_left_shift_12 (
    .a(n8_bit_left_shift_11_a_left_shifted), .over_in(n8_bit_left_shift_11_overflow),
    .a_left_shifted(n8_bit_left_shift_12_a_left_shifted), .overflow(n8_bit_left_shift_12_overflow));
  _8_bit_left_shift u_8_bit_left_shift_13 (
    .a(and_8_1_7_a_and_bbbbbbbb), .over_in(1'b0), .a_left_shifted(n8_bit_left_shift_13_a_left_shifted),
    .overflow(n8_bit_left_shift_13_overflow));
  _8_bit_left_shift u_8_bit_left_shift_14 (
    .a(n8_bit_left_shift_13_a_left_shifted), .over_in(n8_bit_left_shift_13_overflow),
    .a_left_shifted(n8_bit_left_shift_14_a_left_shifted), .overflow(n8_bit_left_shift_14_overflow));
  _8_bit_left_shift u_8_bit_left_shift_15 (
    .a(n8_bit_left_shift_14_a_left_shifted), .over_in(n8_bit_left_shift_14_overflow),
    .a_left_shifted(n8_bit_left_shift_15_a_left_shifted), .overflow(n8_bit_left_shift_15_overflow));
  _8_bit_left_shift u_8_bit_left_shift_16 (
    .a(n8_bit_left_shift_18_a_left_shifted), .over_in(n8_bit_left_shift_18_overflow),
    .a_left_shifted(n8_bit_left_shift_16_a_left_shifted), .overflow(n8_bit_left_shift_16_overflow));
  _8_bit_left_shift u_8_bit_left_shift_17 (
    .a(n8_bit_left_shift_16_a_left_shifted), .over_in(n8_bit_left_shift_16_overflow),
    .a_left_shifted(n8_bit_left_shift_17_a_left_shifted), .overflow(n8_bit_left_shift_17_overflow));
  _8_bit_left_shift u_8_bit_left_shift_18 (
    .a(and_8_1_8_a_and_bbbbbbbb), .over_in(1'b0), .a_left_shifted(n8_bit_left_shift_18_a_left_shifted),
    .overflow(n8_bit_left_shift_18_overflow));
  _8_bit_adder u_8_bit_adder_1 (
    .a(and_8_1_1_a_and_bbbbbbbb), .b(n8_bit_left_shift_1_a_left_shifted), .overflow(n8_bit_adder_1_overflow),
    .a_b(n8_bit_adder_1_a_b));
  _8_bit_left_shift u_8_bit_left_shift_19 (
    .a(n8_bit_left_shift_9_a_left_shifted), .over_in(n8_bit_left_shift_9_overflow),
    .a_left_shifted(n8_bit_left_shift_19_a_left_shifted), .overflow(OV_4));
  _8_bit_left_shift u_8_bit_left_shift_20 (
    .a(n8_bit_left_shift_21_a_left_shifted), .over_in(n8_bit_left_shift_21_overflow),
    .a_left_shifted(n8_bit_left_shift_20_a_left_shifted), .overflow(OV_5));
  _8_bit_left_shift u_8_bit_left_shift_21 (
    .a(n8_bit_left_shift_10_a_left_shifted), .over_in(n8_bit_left_shift_10_overflow),
    .a_left_shifted(n8_bit_left_shift_21_a_left_shifted), .overflow(n8_bit_left_shift_21_overflow));
  _8_bit_left_shift u_8_bit_left_shift_22 (
    .a(n8_bit_left_shift_23_a_left_shifted), .over_in(n8_bit_left_shift_23_overflow),
    .a_left_shifted(n8_bit_left_shift_22_a_left_shifted), .overflow(OV_6));
  _8_bit_left_shift u_8_bit_left_shift_23 (
    .a(n8_bit_left_shift_24_a_left_shifted), .over_in(n8_bit_left_shift_24_overflow),
    .a_left_shifted(n8_bit_left_shift_23_a_left_shifted), .overflow(n8_bit_left_shift_23_overflow));
  _8_bit_left_shift u_8_bit_left_shift_24 (
    .a(n8_bit_left_shift_15_a_left_shifted), .over_in(n8_bit_left_shift_15_overflow),
    .a_left_shifted(n8_bit_left_shift_24_a_left_shifted), .overflow(n8_bit_left_shift_24_overflow));
  _8_bit_left_shift u_8_bit_left_shift_25 (
    .a(n8_bit_left_shift_17_a_left_shifted), .over_in(n8_bit_left_shift_17_overflow),
    .a_left_shifted(n8_bit_left_shift_25_a_left_shifted), .overflow(n8_bit_left_shift_25_overflow));
  _8_bit_left_shift u_8_bit_left_shift_26 (
    .a(n8_bit_left_shift_27_a_left_shifted), .over_in(n8_bit_left_shift_27_overflow),
    .a_left_shifted(n8_bit_left_shift_26_a_left_shifted), .overflow(n8_bit_left_shift_26_overflow));
  _8_bit_left_shift u_8_bit_left_shift_27 (
    .a(n8_bit_left_shift_25_a_left_shifted), .over_in(n8_bit_left_shift_25_overflow),
    .a_left_shifted(n8_bit_left_shift_27_a_left_shifted), .overflow(n8_bit_left_shift_27_overflow));
  _8_bit_adder u_8_bit_adder_2 (
    .a(n8_bit_adder_1_a_b), .b(n8_bit_left_shift_2_a_left_shifted), .overflow(n8_bit_adder_2_overflow),
    .a_b(n8_bit_adder_2_a_b));
  _8_bit_adder u_8_bit_adder_3 (
    .a(n8_bit_adder_2_a_b), .b(n8_bit_left_shift_4_a_left_shifted), .overflow(n8_bit_adder_3_overflow),
    .a_b(n8_bit_adder_3_a_b));
  _8_bit_left_shift u_8_bit_left_shift_28 (
    .a(n8_bit_left_shift_26_a_left_shifted), .over_in(n8_bit_left_shift_26_overflow),
    .a_left_shifted(n8_bit_left_shift_28_a_left_shifted), .overflow(OV_7));
  _8_bit_adder u_8_bit_adder_4 (
    .a(n8_bit_adder_3_a_b), .b(n8_bit_left_shift_19_a_left_shifted), .overflow(n8_bit_adder_4_overflow),
    .a_b(n8_bit_adder_4_a_b));
  _8_bit_adder u_8_bit_adder_5 (
    .a(n8_bit_adder_4_a_b), .b(n8_bit_left_shift_20_a_left_shifted), .overflow(n8_bit_adder_5_overflow),
    .a_b(n8_bit_adder_5_a_b));
  _8_bit_adder u_8_bit_adder_6 (
    .a(n8_bit_adder_5_a_b), .b(n8_bit_left_shift_22_a_left_shifted), .overflow(n8_bit_adder_6_overflow),
    .a_b(n8_bit_adder_6_a_b));
  or or_1 (or_1_out, OV_1, OV_2, OV_3, OV_4, OV_5, OV_6, OV_7);
  or or_2 (or_2_out, n8_bit_adder_1_overflow, n8_bit_adder_2_overflow, n8_bit_adder_3_overflow, n8_bit_adder_4_overflow, n8_bit_adder_5_overflow, n8_bit_adder_6_overflow, n8_bit_adder_7_overflow);
  _8_bit_adder u_8_bit_adder_7 (
    .a(n8_bit_adder_6_a_b), .b(n8_bit_left_shift_28_a_left_shifted), .overflow(n8_bit_adder_7_overflow),
    .a_b(n8_bit_adder_7_a_b));
  _2_s_complement u_2_s_complement_1 (.a(n8_bit_adder_7_a_b), .minus_a(n2_s_complement_1_minus_a));
  or or_3 (overflow, or_1_out, or_2_out);
  // Probe on a_x_b
  Multiplexer #(.width(8)) multiplexer_1 (
    .in0(n8_bit_adder_7_a_b), .in1(n2_s_complement_1_minus_a), .out(a_x_b), .sel(xor_1_out));  // open: en
  xor xor_1 (xor_1_out, a[7], b[7]);

  // Other names for the same wires on the sheet: a___0 = a[7]; b___0 = b[7]
endmodule

// DIV
module _8_bit_divider (
  input  [7:0] a,
  input  [7:0] b,
  output [7:0] quotient_of_a_b,
  output [7:0] remainder_of_a_b,
  output overflow
);

  wire xor_1_out;
  wire [6:0] n8_bit_can_subtract_7__1_if_a___b____0;
  wire [7:0] n2_s_complement_1_minus_a, n2_s_complement_2_minus_a, n8_bit_absolute_1_a_2,
       n8_bit_absolute_2_a_2, n8_bit_can_subtract_1_if_a_b____0__a_b_else__a,
       n8_bit_can_subtract_2_if_a_b____0__a_b_else__a, n8_bit_can_subtract_3_if_a_b____0__a_b_else__a,
       n8_bit_can_subtract_4_if_a_b____0__a_b_else__a, n8_bit_can_subtract_5_if_a_b____0__a_b_else__a,
       n8_bit_can_subtract_6_if_a_b____0__a_b_else__a, n8_bit_can_subtract_7_if_a_b____0__a_b_else__a;

  // Probe on a
  // Probe on b
  _8_bit_absolute u_8_bit_absolute_1 (.a(a), .a_2(n8_bit_absolute_1_a_2));
  _8_bit_absolute u_8_bit_absolute_2 (.a(b), .a_2(n8_bit_absolute_2_a_2));
  _8_bit_iszero u_8_bit_iszero_1 (.a(b), .a____0(overflow));
  _8_bit_can_subtract u_8_bit_can_subtract_1 (
    .a({{7{1'b0}}, n8_bit_absolute_1_a_2[6]}), .b(n8_bit_absolute_2_a_2),
    ._1_if_a___b____0(n8_bit_can_subtract_7__1_if_a___b____0[6]),
    .if_a_b____0__a_b_else__a(n8_bit_can_subtract_1_if_a_b____0__a_b_else__a));
  _8_bit_can_subtract u_8_bit_can_subtract_2 (
    .a({n8_bit_can_subtract_1_if_a_b____0__a_b_else__a[6:0], n8_bit_absolute_1_a_2[5]}),
    .b(n8_bit_absolute_2_a_2), ._1_if_a___b____0(n8_bit_can_subtract_7__1_if_a___b____0[5]),
    .if_a_b____0__a_b_else__a(n8_bit_can_subtract_2_if_a_b____0__a_b_else__a));
  _8_bit_can_subtract u_8_bit_can_subtract_3 (
    .a({n8_bit_can_subtract_2_if_a_b____0__a_b_else__a[6:0], n8_bit_absolute_1_a_2[4]}),
    .b(n8_bit_absolute_2_a_2), ._1_if_a___b____0(n8_bit_can_subtract_7__1_if_a___b____0[4]),
    .if_a_b____0__a_b_else__a(n8_bit_can_subtract_3_if_a_b____0__a_b_else__a));
  _8_bit_can_subtract u_8_bit_can_subtract_4 (
    .a({n8_bit_can_subtract_3_if_a_b____0__a_b_else__a[6:0], n8_bit_absolute_1_a_2[3]}),
    .b(n8_bit_absolute_2_a_2), ._1_if_a___b____0(n8_bit_can_subtract_7__1_if_a___b____0[3]),
    .if_a_b____0__a_b_else__a(n8_bit_can_subtract_4_if_a_b____0__a_b_else__a));
  _8_bit_can_subtract u_8_bit_can_subtract_5 (
    .a({n8_bit_can_subtract_4_if_a_b____0__a_b_else__a[6:0], n8_bit_absolute_1_a_2[2]}),
    .b(n8_bit_absolute_2_a_2), ._1_if_a___b____0(n8_bit_can_subtract_7__1_if_a___b____0[2]),
    .if_a_b____0__a_b_else__a(n8_bit_can_subtract_5_if_a_b____0__a_b_else__a));
  _8_bit_can_subtract u_8_bit_can_subtract_6 (
    .a({n8_bit_can_subtract_5_if_a_b____0__a_b_else__a[6:0], n8_bit_absolute_1_a_2[1]}),
    .b(n8_bit_absolute_2_a_2), ._1_if_a___b____0(n8_bit_can_subtract_7__1_if_a___b____0[1]),
    .if_a_b____0__a_b_else__a(n8_bit_can_subtract_6_if_a_b____0__a_b_else__a));
  _2_s_complement u_2_s_complement_1 (
    .a({1'b0, n8_bit_can_subtract_7__1_if_a___b____0}), .minus_a(n2_s_complement_1_minus_a));
  _8_bit_can_subtract u_8_bit_can_subtract_7 (
    .a({n8_bit_can_subtract_6_if_a_b____0__a_b_else__a[6:0], n8_bit_absolute_1_a_2[0]}),
    .b(n8_bit_absolute_2_a_2), ._1_if_a___b____0(n8_bit_can_subtract_7__1_if_a___b____0[0]),
    .if_a_b____0__a_b_else__a(n8_bit_can_subtract_7_if_a_b____0__a_b_else__a));
  _2_s_complement u_2_s_complement_2 (
    .a(n8_bit_can_subtract_7_if_a_b____0__a_b_else__a), .minus_a(n2_s_complement_2_minus_a));
  Multiplexer #(.width(8)) multiplexer_1 (
    .in0({1'b0, n8_bit_can_subtract_7__1_if_a___b____0}), .in1(n2_s_complement_1_minus_a),
    .out(quotient_of_a_b), .sel(xor_1_out));  // open: en
  xor xor_1 (xor_1_out, a[7], b[7]);
  Multiplexer #(.width(8)) multiplexer_2 (
    .in0(n8_bit_can_subtract_7_if_a_b____0__a_b_else__a), .in1(n2_s_complement_2_minus_a),
    .out(remainder_of_a_b), .sel(a[7]));  // open: en
  // Probe on quotient_of_a_b
  // Probe on remainder_of_a_b

  // Other names for the same wires on the sheet: a___0 = a[7]; b___0 = b[7]
endmodule

// ABS
module _8_bit_absolute (
  input  [7:0] a,
  output [7:0] a_2
);

  wire [7:0] n2_s_complement_1_minus_a;

  // Probe on a
  _2_s_complement u_2_s_complement_1 (.a(a), .minus_a(n2_s_complement_1_minus_a));
  Multiplexer #(.width(8)) multiplexer_1 (.in0(a), .in1(n2_s_complement_1_minus_a), .out(a_2), .sel(a[7]));  // open: en
  // Probe on a_2
endmodule

// =0
module _8_bit_iszero (
  input  [7:0] a,
  output a____0
);

  nor nor_1 (a____0, a[0], a[1], a[2], a[3], a[4], a[5], a[6], a[7]);
endmodule

// CAN-
module _8_bit_can_subtract (
  input  [7:0] a,
  input  [7:0] b,
  output [7:0] if_a_b____0__a_b_else__a,
  output _1_if_a___b____0
);

  wire [7:0] n8_bit_subtractor_1_a_b;

  // Probe on a
  // Probe on b
  _8_bit_subtractor u_8_bit_subtractor_1 (.a(a), .b(b), .a_b(n8_bit_subtractor_1_a_b));  // open: overflow
  not not_1 (_1_if_a___b____0, n8_bit_subtractor_1_a_b[7]);
  // Probe on if_a_b____0__a_b_else__a
  Multiplexer #(.width(8)) multiplexer_1 (
    .in0(a), .in1(n8_bit_subtractor_1_a_b), .out(if_a_b____0__a_b_else__a), .sel(_1_if_a___b____0));  // open: en
endmodule

// LS
module _8_bit_left_shift (
  input  [7:0] a,
  input  over_in,
  output [7:0] a_left_shifted,
  output overflow
);

  wire xor_1_out;

  // Probe on a
  xor xor_1 (xor_1_out, a[6], a[7]);
  // Probe on {a[6:0], 1'b0}
  or or_1 (overflow, xor_1_out, over_in);

  assign a_left_shifted = {a[6:0], 1'b0};
endmodule

// AND
module AND_8_1 (
  input  [7:0] a,
  input  b,
  output [7:0] a_AND_bbbbbbbb
);

  assign a_AND_bbbbbbbb = a & {8{b}};  // AND_Gate and_1, 8 bits wide
endmodule
