// Logisim project instruction_cycle.circ as structural Verilog: 7 circuits, main circuit isLDA
module main (
);

  wire Clock, clock_1_out, CMD, I_O, j_k_ff_1_qn, JMP, LDA, NOP, or_1_out, STA, STP;
  wire [7:0] Adress, multiplexer_1_out, PC_q;
  wire [15:0] Acc, multiplexer_2_out, ram_1_data;
  wire [15:8] IR_q;

  or or_1 (or_1_out, I_O, NOP);
  Clock clock_1 (.out(clock_1_out));
  Counter PC (.load(JMP), .D(Adress), .count(or_1_out), .Q(PC_q), .clk(Clock));  // open: carry, clr
  J_K_Flip_Flop j_k_ff_1 (.J(STP), .clk(clock_1_out), .K(1'b0), .Qn(j_k_ff_1_qn));  // open: Q, preset, en, reset
  Multiplexer #(.width(8)) multiplexer_1 (.in0(PC_q), .in1(Adress), .out(multiplexer_1_out), .sel(I_O));  // open: en
  and and_1 (Clock, clock_1_out, j_k_ff_1_qn);
  RAM #(.dataWidth(16), .bus("separate")) ram_1 (
    .addr(multiplexer_1_out), .din(Acc), .data(ram_1_data), .str(STA), .clk(Clock));  // open: sel, ld, clr
  or or_2 (I_O, STA, LDA);
  Register #(.width(16)) u_ACC (.D(ram_1_data), .en(LDA), .Q(Acc), .clk(Clock));  // open: clr
  Multiplexer #(.width(16)) multiplexer_2 (
    .in0(ram_1_data), .in1({16{1'b0}}), .out(multiplexer_2_out), .sel(CMD));  // open: en
  or or_3 (CMD, I_O, NOP, JMP, STP);
  // Probe on Adress
  Register #(.width(16)) IR (.D(multiplexer_2_out), .Q({IR_q, Adress}), .clk(Clock));  // open: en, clr
  // Probe on IR_q
  isLDA islda_1 (.in_1(IR_q), .out_2(LDA));
  isSTA issta_1 (.in_1(IR_q), .out_2(STA));
  isSTP isstp_1 (.in_1(IR_q), .out_2(STP));
  isJMP isjmp_1 (.in_1(IR_q), .out_2(JMP));
  isNOP isnop_1 (.in_1(IR_q), .out_2(NOP));

  // Notes on the sheet:
  //   Clock
  //   Memória RAM
  //   Controlador
endmodule

// LDA
module isLDA (
  input  [7:0] in_1,
  output out_2
);

  wire [7:0] xor_1_out;

  isZERO iszero_1 (.in_1(xor_1_out), .out_2(out_2));
  assign xor_1_out = in_1 ^ 8'hb;  // XOR_Gate xor_1, 8 bits wide
endmodule

// STP
module isSTP (
  input  [7:0] in_1,
  output out_2
);

  wire [7:0] xor_1_out;

  assign xor_1_out = in_1 ^ 8'h46;  // XOR_Gate xor_1, 8 bits wide
  isZERO iszero_1 (.in_1(xor_1_out), .out_2(out_2));
endmodule

// STA
module isSTA (
  input  [7:0] in_1,
  output out_2
);

  wire [7:0] xor_1_out;

  isZERO iszero_1 (.in_1(xor_1_out), .out_2(out_2));
  assign xor_1_out = in_1 ^ 8'hc;  // XOR_Gate xor_1, 8 bits wide
endmodule

// JMP
module isJMP (
  input  [7:0] in_1,
  output out_2
);

  wire [7:0] xor_1_out;

  assign xor_1_out = in_1 ^ 8'h33;  // XOR_Gate xor_1, 8 bits wide
  isZERO iszero_1 (.in_1(xor_1_out), .out_2(out_2));
endmodule

// NOP
module isNOP (
  input  [7:0] in_1,
  output out_2
);

  wire [7:0] xor_1_out;

  assign xor_1_out = in_1 ^ 8'h32;  // XOR_Gate xor_1, 8 bits wide
  isZERO iszero_1 (.in_1(xor_1_out), .out_2(out_2));
endmodule

// = 0
module isZERO (
  input  [7:0] in_1,
  output out_2
);

  nor nor_1 (out_2, in_1[0], in_1[1], in_1[2], in_1[3], in_1[4], in_1[5], in_1[6], in_1[7]);
endmodule
