// Logisim project instruction_cycle.circ as structural Verilog: 31 circuits, main circuit main
module main (
  input  [15:0] stdin,
  output [15:0] stdout
);

  wire ACC_Access, alu_1_overflow, Clock, clock_1_out, CMD, go_1_out_3, I_O, INN, isjmp_1_out_2,
       isjmp_2_out_2, isnop_1_out_2, isnop_2_out_2, j_k_ff_1_qn, JMP, JMP_prime, JMPC, LDA, NOP, NOP_prime,
       OP, OP_Err, or_2_out, or_3_out, or_6_out, PRN, RAM_Access, STA, STP;
  wire [2:0] \insttoalu_1_instrução_decodificada ;
  wire [5:0] Mask;
  wire [7:0] Address, INST, multiplexer_2_out, multiplexer_3_out, PC_q;
  wire [15:0] Acc, ALU_out, multiplexer_4_out, multiplexer_5_out, RAM_in, RAM_out;

  or or_1 (I_O, STA, INN, PRN, LDA);
  or or_2 (or_2_out, I_O, OP, NOP);
  // Probe on stdin
  Clock clock_1 (.out(clock_1_out));
  or or_3 (or_3_out, STP, OP_Err);
  Register #(.width(16)) register_1 (.D(RAM_out), .en(PRN), .Q(stdout), .clk(Clock));  // open: clr
  Counter PC (.load(JMP), .D(Address), .count(or_2_out), .Q(PC_q), .clk(Clock));  // open: carry, clr
  Multiplexer #(.width(16)) multiplexer_1 (.in0(Acc), .in1(stdin), .out(RAM_in), .sel(INN));  // open: en
  J_K_Flip_Flop j_k_ff_1 (.J(or_3_out), .clk(clock_1_out), .K(1'b0), .Qn(j_k_ff_1_qn));  // open: Q, preset, en, reset
  or or_4 (CMD, I_O, NOP, OP, JMP, STP);
  // Probe on stdout
  Multiplexer #(.width(8)) multiplexer_2 (
    .in0(PC_q), .in1(Address), .out(multiplexer_2_out), .sel(RAM_Access));  // open: en
  and and_1 (Clock, clock_1_out, j_k_ff_1_qn);
  or or_5 (RAM_Access, I_O, OP);
  or or_6 (or_6_out, STA, INN);
  Multiplexer #(.width(8)) multiplexer_3 (
    .in0(8'h32), .in1(8'h33), .out(multiplexer_3_out), .sel(go_1_out_3));  // open: en
  GO go_1 (.\Máscara (Mask), .Tipo_de_jump(INST), .out_3(go_1_out_3));
  or or_7 (ACC_Access, LDA, OP);
  RAM #(.dataWidth(16), .bus("separate")) ram_1 (
    .addr(multiplexer_2_out), .din(RAM_in), .data(RAM_out), .str(or_6_out), .clk(Clock));  // open: sel, ld, clr
  isJMP isjmp_1 (.in_1(multiplexer_3_out), .out_2(isjmp_1_out_2));
  isNOP isnop_1 (.in_1(multiplexer_3_out), .out_2(isnop_1_out_2));
  Multiplexer #(.width(16)) multiplexer_4 (
    .in0(RAM_out), .in1(ALU_out), .out(multiplexer_4_out), .sel(OP));  // open: en
  and and_2 (JMP_prime, isjmp_1_out_2, JMPC);
  and and_3 (NOP_prime, JMPC, isnop_1_out_2);
  InstToALU insttoalu_1 (.\Instrução (INST), .\Instrução_decodificada (\insttoalu_1_instrução_decodificada ));
  ALU alu_1 (
    .a(Acc), .b(RAM_out), .OP(\insttoalu_1_instrução_decodificada ), .overflow(alu_1_overflow),
    .a_OP_b(ALU_out));
  and and_4 (OP_Err, alu_1_overflow, OP);
  Multiplexer #(.width(16)) multiplexer_5 (
    .in0(RAM_out), .in1({16{1'b0}}), .out(multiplexer_5_out), .sel(CMD));  // open: en
  Register #(.width(16)) u_ACC (.D(multiplexer_4_out), .en(ACC_Access), .Q(Acc), .clk(Clock));  // open: clr
  Register #(.width(16)) IR (.D(multiplexer_5_out), .Q({INST, Address}), .clk(Clock));  // open: en, clr
  MSK msk_1 (.\Número (Acc), .\Máscara (Mask));
  // Probe on Address
  // Probe on INST
  isLDA islda_1 (.in_1(INST), .out_2(LDA));
  isSTA issta_1 (.in_1(INST), .out_2(STA));
  isSTP isstp_1 (.in_1(INST), .out_2(STP));
  or or_8 (JMP, JMP_prime, isjmp_2_out_2);
  isJMP isjmp_2 (.in_1(INST), .out_2(isjmp_2_out_2));
  isNOP isnop_2 (.in_1(INST), .out_2(isnop_2_out_2));
  or or_9 (NOP, isnop_2_out_2, NOP_prime);
  isOP isop_1 (.\Instrução (INST), .out_2(OP));
  isINN isinn_1 (.in_1(INST), .out_2(INN));
  isPRN isprn_1 (.in_1(INST), .out_2(PRN));
  isJMPC isjmpc_1 (.\Instrução (INST), .out_2(JMPC));

  // Notes on the sheet:
  //   Clock
  //   Auxiliares
  //   Saída
  //   Entrada
  //   NOP
  //   JMP
  //   Memória RAM
  //   Jump condicional
  //   ALU
  //   Controlador
endmodule

// LDA
module isLDA (
  input  [7:0] in_1,
  output out_2
);

  wire [7:0] xor_1_out;

  isZERO iszero_1 (.in_1(xor_1_out), .out_2(out_2));
  assign xor_1_out = in_1 ^ 8'hb;  // XOR_Gate xor_1, 8 bits wide
endmodule

// STP
module isSTP (
  input  [7:0] in_1,
  output out_2
);

  wire [7:0] xor_1_out;

  assign xor_1_out = in_1 ^ 8'h46;  // XOR_Gate xor_1, 8 bits wide
  isZERO iszero_1 (.in_1(xor_1_out), .out_2(out_2));
endmodule

// STA
module isSTA (
  input  [7:0] in_1,
  output out_2
);

  wire [7:0] xor_1_out;

  isZERO iszero_1 (.in_1(xor_1_out), .out_2(out_2));
  assign xor_1_out = in_1 ^ 8'hc;  // XOR_Gate xor_1, 8 bits wide
endmodule

// JMP
module isJMP (
  input  [7:0] in_1,
  output out_2
);

  wire [7:0] xor_1_out;

  assign xor_1_out = in_1 ^ 8'h33;  // XOR_Gate xor_1, 8 bits wide
  isZERO iszero_1 (.in_1(xor_1_out), .out_2(out_2));
endmodule

// NOP
module isNOP (
  input  [7:0] in_1,
  output out_2
);

  wire [7:0] xor_1_out;

  assign xor_1_out = in_1 ^ 8'h32;  // XOR_Gate xor_1, 8 bits wide
  isZERO iszero_1 (.in_1(xor_1_out), .out_2(out_2));
endmodule

// = 0
module isZERO (
  input  [7:0] in_1,
  output out_2
);

  nor nor_1 (out_2, in_1[0], in_1[1], in_1[2], in_1[3], in_1[4], in_1[5], in_1[6], in_1[7]);
endmodule

// ADD
module isADD (
  input  [7:0] in_1,
  output out_2
);

  wire [7:0] xor_1_out;

  isZERO iszero_1 (.in_1(xor_1_out), .out_2(out_2));
  assign xor_1_out = in_1 ^ 8'h15;  // XOR_Gate xor_1, 8 bits wide
endmodule

// SUB
module isSUB (
  input  [7:0] in_1,
  output out_2
);

  wire [7:0] xor_1_out;

  assign xor_1_out = in_1 ^ 8'h16;  // XOR_Gate xor_1, 8 bits wide
  isZERO iszero_1 (.in_1(xor_1_out), .out_2(out_2));
endmodule

// MUL
module isMUL (
  input  [7:0] in_1,
  output out_2
);

  wire [7:0] xor_1_out;

  isZERO iszero_1 (.in_1(xor_1_out), .out_2(out_2));
  assign xor_1_out = in_1 ^ 8'h17;  // XOR_Gate xor_1, 8 bits wide
endmodule

// DIV
module isDIV (
  input  [7:0] in_1,
  output out_2
);

  wire [7:0] xor_1_out;

  isZERO iszero_1 (.in_1(xor_1_out), .out_2(out_2));
  assign xor_1_out = in_1 ^ 8'h18;  // XOR_Gate xor_1, 8 bits wide
endmodule

// REM
module isREM (
  input  [7:0] in_1,
  output out_2
);

  wire [7:0] xor_1_out;

  assign xor_1_out = in_1 ^ 8'h19;  // XOR_Gate xor_1, 8 bits wide
  isZERO iszero_1 (.in_1(xor_1_out), .out_2(out_2));
endmodule

// OP
module isOP (
  input  [7:0] \Instrução ,
  output out_2
);

  wire isadd_1_out_2, isdiv_1_out_2, ismul_1_out_2, isrem_1_out_2, issub_1_out_2;

  isADD isadd_1 (.in_1(\Instrução ), .out_2(isadd_1_out_2));
  isSUB issub_1 (.in_1(\Instrução ), .out_2(issub_1_out_2));
  isMUL ismul_1 (.in_1(\Instrução ), .out_2(ismul_1_out_2));
  isDIV isdiv_1 (.in_1(\Instrução ), .out_2(isdiv_1_out_2));
  isREM isrem_1 (.in_1(\Instrução ), .out_2(isrem_1_out_2));
  or or_1 (out_2, isadd_1_out_2, issub_1_out_2, ismul_1_out_2, isdiv_1_out_2, isrem_1_out_2);
endmodule

module ALU (
  input  [2:0] OP,
  input  [15:0] a,
  input  [15:0] b,
  output [15:0] a_OP_b,
  output overflow
);

  wire divfix_1_overflow, mulfix_1_overflow, subfix_1_overflow, sumfix_1_overflow;
  wire [15:0] divfix_1_a___b, divfix_1_a___b_2, mulfix_1_a_x_b, subfix_1_a_b, sumfix_1_a_b;

  // Probe on a
  // Probe on b
  SumFix sumfix_1 (.a(a), .b(b), .overflow(sumfix_1_overflow), .a_b(sumfix_1_a_b));
  SubFix subfix_1 (.a(a), .b(b), .overflow(subfix_1_overflow), .a_b(subfix_1_a_b));
  MulFix mulfix_1 (.a(a), .b(b), .overflow(mulfix_1_overflow), .a_x_b(mulfix_1_a_x_b));
  DivFix divfix_1 (.a(a), .b(b), .overflow(divfix_1_overflow), .a___b(divfix_1_a___b), .a___b_2(divfix_1_a___b_2));
  Multiplexer #(.select(3)) multiplexer_1 (
    .in0(sumfix_1_overflow), .in1(subfix_1_overflow), .in2(mulfix_1_overflow), .in3(divfix_1_overflow),
    .in4(divfix_1_overflow), .out(overflow), .sel(OP));  // open: in5, in6, in7, en
  Multiplexer #(.select(3), .width(16)) multiplexer_2 (
    .in0(sumfix_1_a_b), .in1(subfix_1_a_b), .in2(mulfix_1_a_x_b), .in3(divfix_1_a___b),
    .in4(divfix_1_a___b_2), .out(a_OP_b), .sel(OP));  // open: in5, in6, in7, en
  // Probe on a_OP_b
endmodule

// toALU
module InstToALU (
  input  [7:0] \Instrução ,
  output [2:0] \Instrução_decodificada 
);

  wire [7:3] subtractor_1_out;

  Subtractor subtractor_1 (
    .a(\Instrução ), .b(8'h15), .out({subtractor_1_out, \Instrução_decodificada }));  // open: bin, bout
endmodule

// INN
module isINN (
  input  [7:0] in_1,
  output out_2
);

  wire [7:0] xor_1_out;

  assign xor_1_out = in_1 ^ 8'h1f;  // XOR_Gate xor_1, 8 bits wide
  isZERO iszero_1 (.in_1(xor_1_out), .out_2(out_2));
endmodule

// PRN
module isPRN (
  input  [7:0] in_1,
  output out_2
);

  wire [7:0] xor_1_out;

  isZERO iszero_1 (.in_1(xor_1_out), .out_2(out_2));
  assign xor_1_out = in_1 ^ 8'h29;  // XOR_Gate xor_1, 8 bits wide
endmodule

// JLE
module isJLE (
  input  [7:0] in_1,
  output out_2
);

  wire [7:0] xor_1_out;

  isZERO iszero_1 (.in_1(xor_1_out), .out_2(out_2));
  assign xor_1_out = in_1 ^ 8'h34;  // XOR_Gate xor_1, 8 bits wide
endmodule

// JDZ
module isJDZ (
  input  [7:0] in_1,
  output out_2
);

  wire [7:0] xor_1_out;

  isZERO iszero_1 (.in_1(xor_1_out), .out_2(out_2));
  assign xor_1_out = in_1 ^ 8'h35;  // XOR_Gate xor_1, 8 bits wide
endmodule

// JGT
module isJGT (
  input  [7:0] in_1,
  output out_2
);

  wire [7:0] xor_1_out;

  isZERO iszero_1 (.in_1(xor_1_out), .out_2(out_2));
  assign xor_1_out = in_1 ^ 8'h36;  // XOR_Gate xor_1, 8 bits wide
endmodule

// JEQ
module isJEQ (
  input  [7:0] in_1,
  output out_2
);

  wire [7:0] xor_1_out;

  isZERO iszero_1 (.in_1(xor_1_out), .out_2(out_2));
  assign xor_1_out = in_1 ^ 8'h37;  // XOR_Gate xor_1, 8 bits wide
endmodule

// JLT
module isJLT (
  input  [7:0] in_1,
  output out_2
);

  wire [7:0] xor_1_out;

  isZERO iszero_1 (.in_1(xor_1_out), .out_2(out_2));
  assign xor_1_out = in_1 ^ 8'h38;  // XOR_Gate xor_1, 8 bits wide
endmodule

// JGE
module isJGE (
  input  [7:0] in_1,
  output out_2
);

  wire [7:0] xor_1_out;

  assign xor_1_out = in_1 ^ 8'h39;  // XOR_Gate xor_1, 8 bits wide
  isZERO iszero_1 (.in_1(xor_1_out), .out_2(out_2));
endmodule

// JMPC
module isJMPC (
  input  [7:0] \Instrução ,
  output out_2
);

  wire isjdz_1_out_2, isjeq_1_out_2, isjge_1_out_2, isjgt_1_out_2, isjle_1_out_2, isjlt_1_out_2;

  isJLE isjle_1 (.in_1(\Instrução ), .out_2(isjle_1_out_2));
  isJDZ isjdz_1 (.in_1(\Instrução ), .out_2(isjdz_1_out_2));
  isJGT isjgt_1 (.in_1(\Instrução ), .out_2(isjgt_1_out_2));
  isJEQ isjeq_1 (.in_1(\Instrução ), .out_2(isjeq_1_out_2));
  isJLT isjlt_1 (.in_1(\Instrução ), .out_2(isjlt_1_out_2));
  isJGE isjge_1 (.in_1(\Instrução ), .out_2(isjge_1_out_2));
  or or_1 (out_2, isjle_1_out_2, isjdz_1_out_2, isjgt_1_out_2, isjeq_1_out_2, isjlt_1_out_2, isjge_1_out_2);
endmodule

module MSK (
  input  [15:0] \Número ,
  output [5:0] \Máscara 
);

  Comparator #(.width(16)) comparator_1 (
    .a(\Número ), .b({16{1'b0}}), .gt(\Máscara [2]), .eq(\Máscara [3]), .lt(\Máscara [4]));
  or or_1 (\Máscara [0], \Máscara [3], \Máscara [4]);
  or or_2 (\Máscara [1], \Máscara [2], \Máscara [4]);
  or or_3 (\Máscara [5], \Máscara [3], \Máscara [2]);
endmodule

module GO (
  input  [5:0] \Máscara ,
  input  [7:0] Tipo_de_jump,
  output out_3
);

  wire iszero_1_out_2;
  wire [5:0] and_1_out;
  wire [7:0] shifter_1_out, subtractor_1_out;

  Subtractor subtractor_1 (.a(Tipo_de_jump), .b(8'h34), .out(subtractor_1_out));  // open: bin, bout
  Shifter shifter_1 (.in(8'h1), .\dist (subtractor_1_out[2:0]), .out(shifter_1_out));
  assign and_1_out = \Máscara  & shifter_1_out[5:0];  // AND_Gate and_1, 6 bits wide
  isZERO iszero_1 (.in_1({2'b00, and_1_out}), .out_2(iszero_1_out_2));
  not not_1 (out_3, iszero_1_out_2);
endmodule

// +
module SumFix (
  input  [15:0] a,
  input  [15:0] b,
  output [15:0] a_b,
  output overflow
);

  wire adder_1_cout, adder_2_cout;

  // Probe on a
  // Probe on b
  Adder #(.width(15)) adder_1 (.a(a[14:0]), .b(b[14:0]), .out(a_b[14:0]), .cout(adder_1_cout));  // open: cin
  Adder #(.width(1)) adder_2 (.a(b[15]), .b(a[15]), .out(a_b[15]), .cin(adder_1_cout), .cout(adder_2_cout));
  xor xor_1 (overflow, adder_2_cout, adder_1_cout);
  // Probe on a_b
endmodule

// -
module SubFix (
  input  [15:0] a,
  input  [15:0] b,
  output [15:0] a_b,
  output overflow
);

  wire [15:0] negator_1_out;

  // Probe on a
  // Probe on b
  SumFix sumfix_1 (.a(a), .b(negator_1_out), .overflow(overflow), .a_b(a_b));
  Negator #(.width(16)) negator_1 (.in(b), .out(negator_1_out));
  // Probe on a_b
endmodule

// x
module MulFix (
  input  [15:0] a,
  input  [15:0] b,
  output [15:0] a_x_b,
  output overflow
);

  wire comparator_1_eq, xor_1_out;
  wire [14:0] multiplier_1_cout, multiplier_1_out;
  wire [15:0] abs_1_a_2, abs_2_a_2, negator_1_out;

  // Probe on a
  // Probe on b
  ABS abs_1 (.a(a), .a_2(abs_1_a_2));
  ABS abs_2 (.a(b), .a_2(abs_2_a_2));
  Multiplier #(.width(15)) multiplier_1 (
    .a(abs_1_a_2[14:0]), .b(abs_2_a_2[14:0]), .out(multiplier_1_out), .cout(multiplier_1_cout));  // open: cin
  Comparator #(.width(15), .mode("unsigned")) comparator_1 (
    .a(multiplier_1_cout), .b({15{1'b0}}), .eq(comparator_1_eq));  // open: gt, lt
  not not_1 (overflow, comparator_1_eq);
  Negator #(.width(16)) negator_1 (.in({1'b0, multiplier_1_out}), .out(negator_1_out));
  xor xor_1 (xor_1_out, a[15], b[15]);
  // Probe on a_x_b
  Multiplexer #(.width(16)) multiplexer_1 (
    .in0({1'b0, multiplier_1_out}), .in1(negator_1_out), .out(a_x_b), .sel(xor_1_out));  // open: en

  // Other names for the same wires on the sheet: a___0 = a[15]; b___0 = b[15]
endmodule

// /
module DivFix (
  input  [15:0] a,
  input  [15:0] b,
  output [15:0] a___b,
  output overflow,
  output [15:0] a___b_2
);

  wire xor_1_out;
  wire [15:0] abs_1_a_2, abs_2_a_2, divider_1_out, divider_1_rem, negator_1_out, negator_2_out;

  // Probe on a
  // Probe on b
  ABS abs_1 (.a(a), .a_2(abs_1_a_2));
  ABS abs_2 (.a(b), .a_2(abs_2_a_2));
  Comparator #(.width(16), .mode("unsigned")) comparator_1 (.a(b), .b({16{1'b0}}), .eq(overflow));  // open: gt, lt
  Divider #(.width(16)) divider_1 (
    .a(abs_1_a_2), .b(abs_2_a_2), .out(divider_1_out), .rem(divider_1_rem));  // open: upper
  Negator #(.width(16)) negator_1 (.in(divider_1_rem), .out(negator_1_out));
  Multiplexer #(.width(16)) multiplexer_1 (
    .in0(divider_1_rem), .in1(negator_1_out), .out(a___b_2), .sel(a[15]));  // open: en
  Negator #(.width(16)) negator_2 (.in(divider_1_out), .out(negator_2_out));
  // Probe on a___b_2
  Multiplexer #(.width(16)) multiplexer_2 (
    .in0(divider_1_out), .in1(negator_2_out), .out(a___b), .sel(xor_1_out));  // open: en
  xor xor_1 (xor_1_out, a[15], b[15]);
  // Probe on a___b

  // Other names for the same wires on the sheet: a___0 = a[15]; b___0 = b[15]
endmodule

module ABS (
  input  [15:0] a,
  output [15:0] a_2
);

  wire [15:0] negator_1_out;

  // Probe on a
  Negator #(.width(16)) negator_1 (.in(a), .out(negator_1_out));
  Multiplexer #(.width(16)) multiplexer_1 (.in0(a), .in1(negator_1_out), .out(a_2), .sel(a[15]));  // open: en
  // Probe on a_2
endmodule
