// Logisim project Chiclete.circ as structural Verilog: 1 circuit, main circuit main
module main (
  input  d,
  input  c,
  output out_3
);

  wire and_1_out, and_2_out, and_3_out, and_6_out, and_7_out, and_8_out, and_9_out, and_10_out, and_11_out,
       and_12_out, and_13_out, button_1_out, d_nc, J0, J1, K0, K1, ndc, not_1_out, not_2_out, not_3_out, ny0,
       ny1, y0, y1;

  not not_1 (not_1_out, d);
  and and_1 (and_1_out, d, y0);
  or or_1 (out_3, and_1_out, and_3_out, and_2_out);
  not not_2 (not_2_out, c);
  not not_3 (not_3_out, not_2_out);
  and and_2 (and_2_out, not_3_out, y1, y0);
  and and_3 (and_3_out, d, not_3_out, ny1);
  and and_4 (d_nc, d, not_2_out);
  and and_5 (ndc, not_3_out, not_1_out);
  J_K_Flip_Flop _1 (.J(J1), .clk(button_1_out), .K(K1), .Q(y1), .Qn(ny1));  // open: preset, en, reset
  Button button_1 (.out(button_1_out));
  and and_6 (and_6_out, ndc, y0);
  and and_7 (and_7_out, ny1, d_nc, ny0);
  and and_8 (and_8_out, ndc, y0);
  and and_9 (and_9_out, d_nc, ny0);
  or or_2 (J1, and_6_out, and_7_out);
  or or_3 (K1, and_8_out, and_9_out);
  J_K_Flip_Flop _0 (.J(J0), .clk(button_1_out), .K(K0), .Q(y0), .Qn(ny0));  // open: preset, en, reset
  and and_10 (and_10_out, ndc, ny1);
  and and_11 (and_11_out, ny1, d_nc);
  and and_12 (and_12_out, d_nc, ny1);
  and and_13 (and_13_out, y1, ndc, y0);
  or or_4 (J0, and_10_out, and_11_out);
  or or_5 (K0, and_12_out, and_13_out);
endmodule
