// Logisim project PrimeNumber.circ as structural Verilog: 1 circuit, main circuit main
module main (
  input  a3,
  input  a2,
  input  a1,
  input  a0,
  output out_5
);

  wire and_1_out, and_2_out, and_3_out, and_4_out, and_5_out, not_1_out, not_2_out, or_1_out, xor_1_out;

  not not_1 (not_1_out, a2);
  and and_1 (and_1_out, a3, a0);
  and and_2 (and_2_out, a1, not_1_out);
  and and_3 (and_3_out, a2, a0);
  not not_2 (not_2_out, a3);
  xor xor_1 (xor_1_out, a2, a1);
  or or_1 (or_1_out, and_2_out, and_3_out);
  and and_4 (and_4_out, and_1_out, xor_1_out);
  and and_5 (and_5_out, or_1_out, not_2_out);
  or or_2 (out_5, and_4_out, and_5_out);
endmodule
