// Logisim project camera.circ as structural Verilog: 1 circuit, main circuit main
module main (
  input  X,
  input  Y,
  output z
);

  wire a0_q, a0_qn, a1_q, a1_qn, and_1_out, and_2_out, and_3_out, and_4_out, and_5_out, button_1_out,
       not_1_out, not_2_out, or_1_out, or_2_out;

  not not_1 (not_1_out, X);
  and and_1 (and_1_out, X, Y, a0_qn, a1_qn);
  and and_2 (and_2_out, a0_q, not_1_out, Y);
  or or_1 (or_1_out, and_1_out, and_2_out);
  or or_2 (or_2_out, and_2_out, and_3_out);
  and and_3 (and_3_out, X, a0_q);
  not not_2 (not_2_out, X);
  and and_4 (and_4_out, a1_qn, X);
  and and_5 (and_5_out, a0_q, X);
  Button button_1 (.out(button_1_out));
  J_K_Flip_Flop a1 (.J(or_1_out), .clk(button_1_out), .K(or_2_out), .Q(a1_q), .Qn(a1_qn));  // open: preset, en, reset
  J_K_Flip_Flop a0 (.J(and_4_out), .clk(button_1_out), .K(and_5_out), .Q(a0_q), .Qn(a0_qn));  // open: preset, en, reset
  and and_6 (z, not_2_out, Y, a1_q, a0_q);
endmodule
