// Logisim project paridade.circ as structural Verilog: 1 circuit, main circuit main
module main (
  input  in_1,
  output out_2
);

  wire and_1_out, and_2_out, button_1_out, j_k_ff_1_q, j_k_ff_1_qn, not_1_out;

  J_K_Flip_Flop j_k_ff_1 (
    .J(in_1), .clk(button_1_out), .K(in_1), .Q(j_k_ff_1_q), .Qn(j_k_ff_1_qn));  // open: preset, en, reset
  Button button_1 (.out(button_1_out));
  not not_1 (not_1_out, in_1);
  and and_1 (and_1_out, in_1, j_k_ff_1_q);
  and and_2 (and_2_out, j_k_ff_1_qn, not_1_out);
  or or_1 (out_2, and_1_out, and_2_out);
endmodule
